# Fritzing sketch Puerta (saved by Fritzing 0.9.3b)
breadboards: 1

parts:
  U1 = LCD-16X2 [package=lcd-16x2]
  R1 = Rotary Potentiometer (Large) [maximum_resistance=100kΩ package=THT]
  S1 = Reed switch [package=THT]
  J1 = Piezo Speaker
  Componente1 = Arduino Uno (Rev3) - ICSP
  R2 = Resistor [tolerance=±5% resistance=1k package="2512 [SMD]"]  # not connected

nets:
  VSS: U1.VSS, U1.R_W, U1.K, R1.leg1, S1.pin_2, J1.pin1, Componente1.GND
  VDD: U1.VDD, U1.A, R1.leg2, Componente1.5V
  N1: U1.VO, R1.wiper
  N2: U1.RS, Componente1.D1/TX
  N3: U1.E, Componente1.D2
  N4: U1.DB4, Componente1.D4
  N5: U1.DB5, Componente1.D5_PWM
  N6: U1.DB6, Componente1.D6_PWM
  N7: U1.DB7, Componente1.D7
  N8: S1.pin_1, Componente1.D8
  N9: J1.pin2, Componente1.D9_PWM
